// Digital circuit ALUD.dig as structural Verilog
module ALUD (
  input  CI,
  input  [7:0] A,
  input  [7:0] B,
  input  [3:0] S,
  input  nLOE,
  input  nHOE,
  output [7:0] Q,
  output CO
);

  wire [6:0] ALUDH_d;
  wire [7:0] ALUDL_d;

  EEPROM #(.AddrBits(13), .isProgramMemory("true"), .Bits(8)) ALUDL (
    .A({CI, S, B[3:0], A[3:0]}), .CS(~1'b0), .WE(~1'b1), .OE(~1'b0), .D(ALUDL_d));
  EEPROM #(.AddrBits(13), .isProgramMemory("true"), .Bits(8)) ALUDH (
    .A({ALUDL_d[7], S, B[7:4], A[7:4]}), .CS(~1'b0), .WE(~1'b1), .OE(~1'b0), .D({CO, ALUDH_d}));
  assign Q = ~nLOE ? {ALUDH_d[3:0], ALUDL_d[3:0]} : 8'bz;  // DriverInvSel driverinvsel_1
  assign Q = ~nHOE ? {CO, ALUDH_d[6:4], ALUDL_d[7:4]} : 8'bz;  // DriverInvSel driverinvsel_2

  // Notes on the sheet:
  //   nLOE: default 1
  //   nHOE: default 1
  //   contents of ALUDL (hex, n*v repeats v):
  //   10,21,42,83,4,5,6,7,18,29,4a,8b,c,d,e,f,1,30,53,92,15,14,17,16,9,38,5b,9a,1d,1c,1f,
  //   1e,32,3,60,a1,26,27,24,25,3a,b,68,a9,2e,2f,2c,2d,23,12,71,b0,37,36,35,34,2b,1a,79,
  //   b8,3f,3e,3d,3c,54,65,6,c7,40,41,42,43,5c,6d,e,cf,48,49,4a,4b,45,74,17,d6,51,50,53,
  //   52,4d,7c,1f,de,59,58,5b,5a,76,47,24,e5,62,63,60,61,7e,4f,2c,ed,6a,6b,68,69,67,56,
  //   35,f4,73,72,71,70,6f,5e,3d,fc,7b,7a,79,78,98,a9,ca,b,8c,8d,8e,8f,90,a1,c2,3,84,85,
  //   86,87,89,b8,db,1a,9d,9c,9f,9e,81,b0,d3,12,95,94,97,96,ba,8b,e8,29,ae,af,ac,ad,b2,
  //   83,e0,21,a6,a7,a4,a5,ab,9a,f9,38,bf,be,bd,bc,a3,92,f1,30,b7,b6,b5,b4,dc,ed,8e,4f,
  //   c8,c9,ca,cb,d4,e5,86,47,c0,c1,c2,c3,cd,fc,9f,5e,d9,d8,db,da,c5,f4,97,56,d1,d0,d3,
  //   d2,fe,cf,ac,6d,ea,eb,e8,e9,f6,c7,a4,65,e2,e3,e0,e1,ef,de,bd,7c,fb,fa,f9,f8,e7,d6,
  //   b5,74,f3,f2,f1,f0,0,1,2,3,4,5,6,7,8,9,80,81,82,83,84,85,0,1,2,3,4,5,6,7,8,9,80,81,
  //   82,83,84,85,0,1,2,3,4,5,6,7,8,9,80,81,82,83,84,85,0,1,2,3,4,5,6,7,8,9,80,81,82,83,
  //   84,85,0,1,2,3,4,5,6,7,8,9,80,81,82,83,84,85,0,1,2,3,4,5,6,7,8,9,80,81,82,83,84,85,
  //   0,1,2,3,4,5,6,7,8,9,80,81,82,83,84,85,0,1,2,3,4,5,6,7,8,9,80,81,82,83,84,85,6,7,48,
  //   49,4a,4b,4c,4d,e,f,80,81,82,83,84,85,6,7,48,49,4a,4b,4c,4d,e,f,80,81,82,83,84,85,
  //   6,7,48,49,4a,4b,4c,4d,e,f,80,81,82,83,84,85,6,7,48,49,4a,4b,4c,4d,e,f,80,81,82,83,
  //   84,85,6,7,48,49,4a,4b,4c,4d,e,f,80,81,82,83,84,85,6,7,48,49,4a,4b,4c,4d,e,f,80,81,
  //   82,83,84,85,6,7,48,49,4a,4b,4c,4d,e,f,80,81,82,83,84,85,6,7,48,49,4a,4b,4c,4d,e,f,
  //   80,81,82,83,84,85,0,1,2,3,4,5,6,7,8,9,a,b,c,d,e,f,1,2,3,4,5,6,7,48,9,a,b,c,d,e,f,
  //   80,2,3,4,5,6,7,48,49,a,b,c,d,e,f,80,81,3,4,5,6,7,48,49,4a,b,c,d,e,f,80,81,82,4,5,
  //   6,7,48,49,4a,4b,c,d,e,f,80,81,82,83,5,6,7,48,49,4a,4b,4c,d,e,f,80,81,82,83,84,6,7,
  //   48,49,4a,4b,4c,4d,e,f,80,81,82,83,84,85,7,48,49,4a,4b,4c,4d,4e,f,80,81,82,83,84,85,
  //   86,8,9,a,b,c,d,e,f,c0,c1,c2,c3,c4,c5,c6,c7,9,a,b,c,d,e,f,80,c1,c2,c3,c4,c5,c6,c7,
  //   88,a,b,c,d,e,f,80,81,c2,c3,c4,c5,c6,c7,88,89,b,c,d,e,f,80,81,82,c3,c4,c5,c6,c7,88,
  //   89,8a,c,d,e,f,80,81,82,83,c4,c5,c6,c7,88,89,8a,8b,d,e,f,80,81,82,83,84,c5,c6,c7,88,
  //   89,8a,8b,8c,e,f,80,81,82,83,84,85,c6,c7,88,89,8a,8b,8c,8d,f,80,81,82,83,84,85,86,
  //   c7,88,89,8a,8b,8c,8d,8e,0,1,2,3,4,5,6,7,8,9,a,b,c,d,e,f,8f,0,1,2,3,4,5,6,47,8,9,a,
  //   b,c,d,e,8e,8f,0,1,2,3,4,5,46,47,8,9,a,b,c,d,8d,8e,8f,0,1,2,3,4,45,46,47,8,9,a,b,c,
  //   8c,8d,8e,8f,0,1,2,3,44,45,46,47,8,9,a,b,8b,8c,8d,8e,8f,0,1,2,43,44,45,46,47,8,9,a,
  //   8a,8b,8c,8d,8e,8f,0,1,42,43,44,45,46,47,8,9,89,8a,8b,8c,8d,8e,8f,0,41,42,43,44,45,
  //   46,47,8,c8,c9,ca,cb,cc,cd,ce,cf,0,1,2,3,4,5,6,7,87,c8,c9,ca,cb,cc,cd,ce,8f,0,1,2,
  //   3,4,5,6,86,87,c8,c9,ca,cb,cc,cd,8e,8f,0,1,2,3,4,5,85,86,87,c8,c9,ca,cb,cc,8d,8e,8f,
  //   0,1,2,3,4,84,85,86,87,c8,c9,ca,cb,8c,8d,8e,8f,0,1,2,3,83,84,85,86,87,c8,c9,ca,8b,
  //   8c,8d,8e,8f,0,1,2,82,83,84,85,86,87,c8,c9,8a,8b,8c,8d,8e,8f,0,1,81,82,83,84,85,86,
  //   87,c8,89,8a,8b,8c,8d,8e,8f,0,0,81,82,3,84,5,6,87,88,9,a,8b,c,8d,8e,f,0,81,82,3,84,
  //   5,6,87,88,9,a,8b,c,8d,8e,f,0,81,82,3,84,5,6,87,88,9,a,8b,c,8d,8e,f,0,81,82,3,84,5,
  //   6,87,88,9,a,8b,c,8d,8e,f,0,81,82,3,84,5,6,87,88,9,a,8b,c,8d,8e,f,0,81,82,3,84,5,6,
  //   87,88,9,a,8b,c,8d,8e,f,0,81,82,3,84,5,6,87,88,9,a,8b,c,8d,8e,f,0,81,82,3,84,5,6,87,
  //   88,9,a,8b,c,8d,8e,f,0,81,82,3,84,5,6,87,88,9,a,8b,c,8d,8e,f,0,81,82,3,84,5,6,87,88,
  //   9,a,8b,c,8d,8e,f,0,81,82,3,84,5,6,87,88,9,a,8b,c,8d,8e,f,0,81,82,3,84,5,6,87,88,9,
  //   a,8b,c,8d,8e,f,0,81,82,3,84,5,6,87,88,9,a,8b,c,8d,8e,f,0,81,82,3,84,5,6,87,88,9,a,
  //   8b,c,8d,8e,f,0,81,82,3,84,5,6,87,88,9,a,8b,c,8d,8e,f,0,81,82,3,84,5,6,87,88,9,a,8b,
  //   c,8d,8e,f,0,11,20,31,40,51,60,71,80,91,a0,b1,c0,d1,e0,f1,10,11,30,31,50,51,70,71,
  //   90,91,b0,b1,d0,d1,f0,f1,20,31,20,31,60,71,60,71,a0,b1,a0,b1,e0,f1,e0,f1,30,31,30,
  //   31,70,71,70,71,b0,b1,b0,b1,f0,f1,f0,f1,40,51,60,71,40,51,60,71,c0,d1,e0,f1,c0,d1,
  //   e0,f1,50,51,70,71,50,51,70,71,d0,d1,f0,f1,d0,d1,f0,f1,60,71,60,71,60,71,60,71,e0,
  //   f1,e0,f1,e0,f1,e0,f1,70,71,70,71,70,71,70,71,f0,f1,f0,f1,f0,f1,f0,f1,88,99,a8,b9,
  //   c8,d9,e8,f9,88,99,a8,b9,c8,d9,e8,f9,98,99,b8,b9,d8,d9,f8,f9,98,99,b8,b9,d8,d9,f8,
  //   f9,a8,b9,a8,b9,e8,f9,e8,f9,a8,b9,a8,b9,e8,f9,e8,f9,b8,b9,b8,b9,f8,f9,f8,f9,b8,b9,
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  //   contents of ALUDH (hex, n*v repeats v):
  //   0,1,2,3,14,25,46,87,8,9,a,b,1c,2d,4e,8f,11,10,13,12,5,34,57,96,19,18,1b,1a,d,3c,5f,
  //   9e,22,23,20,21,36,7,64,a5,2a,2b,28,29,3e,f,6c,ad,33,32,31,30,27,16,75,b4,3b,3a,39,
  //   38,2f,1e,7d,bc,44,45,46,47,50,61,2,c3,4c,4d,4e,4f,58,69,a,cb,55,54,57,56,41,70,13,
  //   d2,5d,5c,5f,5e,49,78,1b,da,66,67,64,65,72,43,20,e1,6e,6f,6c,6d,7a,4b,28,e9,77,76,
  //   75,74,63,52,31,f0,7f,7e,7d,7c,6b,5a,39,f8,88,89,8a,8b,9c,ad,ce,f,80,81,82,83,94,a5,
  //   c6,7,99,98,9b,9a,8d,bc,df,1e,91,90,93,92,85,b4,d7,16,aa,ab,a8,a9,be,8f,ec,2d,a2,a3,
  //   a0,a1,b6,87,e4,25,bb,ba,b9,b8,af,9e,fd,3c,b3,b2,b1,b0,a7,96,f5,34,cc,cd,ce,cf,d8,
  //   e9,8a,4b,c4,c5,c6,c7,d0,e1,82,43,dd,dc,df,de,c9,f8,9b,5a,d5,d4,d7,d6,c1,f0,93,52,
  //   ee,ef,ec,ed,fa,cb,a8,69,e6,e7,e4,e5,f2,c3,a0,61,ff,fe,fd,fc,eb,da,b9,78,f7,f6,f5,
  //   f4,e3,d2,b1,70,0,1,2,3,4,5,6,7,8,9,80,81,82,83,84,85,0,1,2,3,4,5,6,7,8,9,80,81,82,
  //   83,84,85,0,1,2,3,4,5,6,7,8,9,80,81,82,83,84,85,0,1,2,3,4,5,6,7,8,9,80,81,82,83,84,
  //   85,0,1,2,3,4,5,6,7,8,9,80,81,82,83,84,85,0,1,2,3,4,5,6,7,8,9,80,81,82,83,84,85,0,
  //   1,2,3,4,5,6,7,8,9,80,81,82,83,84,85,0,1,2,3,4,5,6,7,8,9,80,81,82,83,84,85,6,7,48,
  //   49,4a,4b,4c,4d,e,f,80,81,82,83,84,85,6,7,48,49,4a,4b,4c,4d,e,f,80,81,82,83,84,85,
  //   6,7,48,49,4a,4b,4c,4d,e,f,80,81,82,83,84,85,6,7,48,49,4a,4b,4c,4d,e,f,80,81,82,83,
  //   84,85,6,7,48,49,4a,4b,4c,4d,e,f,80,81,82,83,84,85,6,7,48,49,4a,4b,4c,4d,e,f,80,81,
  //   82,83,84,85,6,7,48,49,4a,4b,4c,4d,e,f,80,81,82,83,84,85,6,7,48,49,4a,4b,4c,4d,e,f,
  //   80,81,82,83,84,85,0,1,2,3,4,5,6,7,8,9,a,b,c,d,e,f,1,2,3,4,5,6,7,48,9,a,b,c,d,e,f,
  //   80,2,3,4,5,6,7,48,49,a,b,c,d,e,f,80,81,3,4,5,6,7,48,49,4a,b,c,d,e,f,80,81,82,4,5,
  //   6,7,48,49,4a,4b,c,d,e,f,80,81,82,83,5,6,7,48,49,4a,4b,4c,d,e,f,80,81,82,83,84,6,7,
  //   48,49,4a,4b,4c,4d,e,f,80,81,82,83,84,85,7,48,49,4a,4b,4c,4d,4e,f,80,81,82,83,84,85,
  //   86,8,9,a,b,c,d,e,f,c0,c1,c2,c3,c4,c5,c6,c7,9,a,b,c,d,e,f,80,c1,c2,c3,c4,c5,c6,c7,
  //   88,a,b,c,d,e,f,80,81,c2,c3,c4,c5,c6,c7,88,89,b,c,d,e,f,80,81,82,c3,c4,c5,c6,c7,88,
  //   89,8a,c,d,e,f,80,81,82,83,c4,c5,c6,c7,88,89,8a,8b,d,e,f,80,81,82,83,84,c5,c6,c7,88,
  //   89,8a,8b,8c,e,f,80,81,82,83,84,85,c6,c7,88,89,8a,8b,8c,8d,f,80,81,82,83,84,85,86,
  //   c7,88,89,8a,8b,8c,8d,8e,0,1,2,3,4,5,6,7,8,9,a,b,c,d,e,f,8f,0,1,2,3,4,5,6,47,8,9,a,
  //   b,c,d,e,8e,8f,0,1,2,3,4,5,46,47,8,9,a,b,c,d,8d,8e,8f,0,1,2,3,4,45,46,47,8,9,a,b,c,
  //   8c,8d,8e,8f,0,1,2,3,44,45,46,47,8,9,a,b,8b,8c,8d,8e,8f,0,1,2,43,44,45,46,47,8,9,a,
  //   8a,8b,8c,8d,8e,8f,0,1,42,43,44,45,46,47,8,9,89,8a,8b,8c,8d,8e,8f,0,41,42,43,44,45,
  //   46,47,8,c8,c9,ca,cb,cc,cd,ce,cf,0,1,2,3,4,5,6,7,87,c8,c9,ca,cb,cc,cd,ce,8f,0,1,2,
  //   3,4,5,6,86,87,c8,c9,ca,cb,cc,cd,8e,8f,0,1,2,3,4,5,85,86,87,c8,c9,ca,cb,cc,8d,8e,8f,
  //   0,1,2,3,4,84,85,86,87,c8,c9,ca,cb,8c,8d,8e,8f,0,1,2,3,83,84,85,86,87,c8,c9,ca,8b,
  //   8c,8d,8e,8f,0,1,2,82,83,84,85,86,87,c8,c9,8a,8b,8c,8d,8e,8f,0,1,81,82,83,84,85,86,
  //   87,c8,89,8a,8b,8c,8d,8e,8f,0,0,81,82,3,84,5,6,87,88,9,a,8b,c,8d,8e,f,0,81,82,3,84,
  //   5,6,87,88,9,a,8b,c,8d,8e,f,0,81,82,3,84,5,6,87,88,9,a,8b,c,8d,8e,f,0,81,82,3,84,5,
  //   6,87,88,9,a,8b,c,8d,8e,f,0,81,82,3,84,5,6,87,88,9,a,8b,c,8d,8e,f,0,81,82,3,84,5,6,
  //   87,88,9,a,8b,c,8d,8e,f,0,81,82,3,84,5,6,87,88,9,a,8b,c,8d,8e,f,0,81,82,3,84,5,6,87,
  //   88,9,a,8b,c,8d,8e,f,0,81,82,3,84,5,6,87,88,9,a,8b,c,8d,8e,f,0,81,82,3,84,5,6,87,88,
  //   9,a,8b,c,8d,8e,f,0,81,82,3,84,5,6,87,88,9,a,8b,c,8d,8e,f,0,81,82,3,84,5,6,87,88,9,
  //   a,8b,c,8d,8e,f,0,81,82,3,84,5,6,87,88,9,a,8b,c,8d,8e,f,0,81,82,3,84,5,6,87,88,9,a,
  //   8b,c,8d,8e,f,0,81,82,3,84,5,6,87,88,9,a,8b,c,8d,8e,f,0,81,82,3,84,5,6,87,88,9,a,8b,
  //   c,8d,8e,f,0,10,20,30,40,50,60,70,80,90,a0,b0,c0,d0,e0,f0,11,11,31,31,51,51,71,71,
  //   91,91,b1,b1,d1,d1,f1,f1,20,30,20,30,60,70,60,70,a0,b0,a0,b0,e0,f0,e0,f0,31,31,31,
  //   31,71,71,71,71,b1,b1,b1,b1,f1,f1,f1,f1,40,50,60,70,40,50,60,70,c0,d0,e0,f0,c0,d0,
  //   e0,f0,51,51,71,71,51,51,71,71,d1,d1,f1,f1,d1,d1,f1,f1,60,70,60,70,60,70,60,70,e0,
  //   f0,e0,f0,e0,f0,e0,f0,71,71,71,71,71,71,71,71,f1,f1,f1,f1,f1,f1,f1,f1,80,90,a0,b0,
  //   c0,d0,e0,f0,80,90,a0,b0,c0,d0,e0,f0,91,91,b1,b1,d1,d1,f1,f1,91,91,b1,b1,d1,d1,f1,
  //   f1,a0,b0,a0,b0,e0,f0,e0,f0,a0,b0,a0,b0,e0,f0,e0,f0,b1,b1,b1,b1,f1,f1,f1,f1,b1,b1,
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endmodule
