// Digital circuit CORE.dig as structural Verilog
module CORE (
  input  clk,
  input  RST,
  input  CLR,
  input  in_4,
  input  [11:0] MIPCBI,
  input  [15:0] PCBI,
  input  MIPCBE,
  input  PCBE
);

  wire ALUD_CO, ALUDH_OE, ALUDL_OE, ALUS_OE, and_3_out, and_4_out, ASSERT_p5, BR_Q, button_1_out, CLK_t,
       CLKR, comparator_1_eq, comparator_1_gt, comparator_1_lt, comparator_2_eq, comparator_3_eq,
       decoder_1_out_0, decoder_1_out_1, decoder_1_out_2, decoder_1_out_3, decoder_1_out_4, decoder_1_out_5,
       decoder_1_out_6, decoder_1_out_7, DIRECT_OE, DIRECT_WE, DPC_JUMP, DUMP_p5, EXT_p5, IRQ_CLR, IRQ_OE,
       nCLR, nDPC_JUMP, nIMMED_OE, not_8_out, not_13_out, nRAM_OE, nROM_OE, nXRAM_OE, or_1_out, RAM_OE,
       RAM_WE, RF_HWE, RF_LWE, RF_SFR, RFSRCR_WE, SFR_OE, SR_WE, WR_WE, XRAM_WE;
  wire [2:0] BR_SRC, BUS_SRC, JUMP_TYPE;
  wire [3:0] ALUSD_FUNC, multiplexer_2_out, RF_SRC;
  wire [5:4] multiplexer_2_out_2;
  wire [6:0] and_2_out;
  wire [7:0] BUS_D, IMMED, RF_Q;
  wire [7:4] RFSRCR_q;
  wire [11:0] ADDRESS, MIPC;
  wire [15:0] ADDR_16, PCER_q;
  wire [47:46] DECODER_2_d;

  Comparator #(.Bits(8)) comparator_1 (
    .a(RF_Q), .b(IMMED), .gt(comparator_1_gt), .eq(comparator_1_eq), .lt(comparator_1_lt));
  Decoder #(.Selector_Bits(3)) decoder_1 (
    .sel(BUS_SRC), .out_0(decoder_1_out_0), .out_1(decoder_1_out_1), .out_2(decoder_1_out_2),
    .out_3(decoder_1_out_3), .out_4(decoder_1_out_4), .out_5(decoder_1_out_5), .out_6(decoder_1_out_6),
    .out_7(decoder_1_out_7));
  not not_1 (ALUS_OE, decoder_1_out_0);
  not not_2 (ALUDL_OE, decoder_1_out_1);
  not not_3 (ALUDH_OE, decoder_1_out_2);
  not not_4 (nIMMED_OE, decoder_1_out_3);
  not not_5 (nRAM_OE, decoder_1_out_4);
  not not_6 (nXRAM_OE, decoder_1_out_5);
  not not_7 (nROM_OE, decoder_1_out_6);
  not not_8 (not_8_out, decoder_1_out_7);
  DCOUTER #(.generic("Bits := 12;")) dcouter_1 (
    .CLK(CLK_t), .CLR(nCLR), .CNT(1'b1), .LE(nDPC_JUMP), .D(ADDRESS), .Q(MIPC));
  Multiplexer #(.Selector_Bits(3)) multiplexer_1 (
    .sel(JUMP_TYPE), .in_0(1'b0), .in_1(1'b1), .in_2(comparator_1_gt), .in_3(comparator_1_eq),
    .in_4(comparator_1_lt), .in_5(BR_Q), .in_6(RST), .in_7(1'b0), .out(DPC_JUMP));
  not not_9 (IRQ_OE, not_8_out);
  assign BUS_D[0] = ~nIMMED_OE ? IMMED[0] : 1'bz;  // DriverInvSel driverinvsel_1
  PullDown #(.Bits(8)) pulldown_1 (.out(BUS_D));
  assign BUS_D = SFR_OE ? RF_Q : 8'bz;  // Driver driver_1
  PCE PCER (.CLK(CLK_t), .D(BUS_D), .RS(RF_SRC), .LWE(RF_LWE), .HWE(RF_HWE), .Q(PCER_q));
  not not_10 (nDPC_JUMP, DPC_JUMP);
  not not_11 (RAM_OE, nRAM_OE);
  // Probe on BUS_D
  ROM #(.AddrBits(12), .Bits(48)) DECODER_2 (
    .A(MIPC), .sel(1'b1),
    .D({DECODER_2_d, IMMED, ADDRESS, JUMP_TYPE, IRQ_CLR, ALUSD_FUNC, XRAM_WE, RAM_WE, RFSRCR_WE, BR_SRC, SR_WE, WR_WE, BUS_SRC, RF_SFR, RF_HWE, RF_LWE, RF_SRC}));
  Register #(.Bits(8)) RFSRCR (.D(BUS_D), .C(CLK_t), .en(RFSRCR_WE), .Q({RFSRCR_q, and_2_out[3:0]}));
  and and_1 (and_2_out[5], RFSRCR_q[4], RAM_WE);
  and and_2 (and_2_out[6], RFSRCR_q[4], RAM_OE);
  Comparator #(.Bits(12)) comparator_2 (.a(MIPCBI), .b(MIPC), .eq(comparator_2_eq));  // open: gt, lt
  Comparator #(.Bits(16)) comparator_3 (.a(PCBI), .b(PCER_q), .eq(comparator_3_eq));  // open: gt, lt
  and and_3 (and_3_out, comparator_2_eq, MIPCBE);
  and and_4 (and_4_out, comparator_3_eq, PCBE);
  Multiplexer #(.Bits(7)) multiplexer_2 (
    .sel(RF_SFR), .in_0({1'b0, RF_HWE, RF_LWE, RF_SRC}),
    .in_1({and_2_out[6:5], and_2_out[5], and_2_out[3:0]}),
    .out({SFR_OE, multiplexer_2_out_2, multiplexer_2_out}));
  // Probe on MIPC
  // Probe on RF_SRC
  // Probe on RF_LWE
  // Probe on RF_HWE
  // Probe on RF_SFR
  // Probe on BUS_SRC
  // Probe on WR_WE
  // Probe on SR_WE
  // Probe on BR_SRC
  // Probe on RFSRCR_WE
  // Probe on RAM_WE
  // Probe on XRAM_WE
  // Probe on ALUSD_FUNC
  // Probe on IRQ_CLR
  // Probe on JUMP_TYPE
  // Probe on ADDRESS
  // Probe on IMMED
  // EXTCTL EXT: pin names not known; wires that end beside it: DIRECT_WE, ADDR_16[15:8], BUS_D, CLK_t, EXT_p5
  // ASSERT ASSERT: pin names not known; wires that end beside it: CLK_t, BUS_D, ADDR_16[15:8], DIRECT_WE, ASSERT_p5, CLK_t
  not not_12 (nCLR, CLR);
  Button button_1 (.out(button_1_out));
  // reg_file RF: pin names not known; wires that end beside it: CLK_t, multiplexer_2_out, BUS_D, multiplexer_2_out_2[4], multiplexer_2_out_2[5], RF_Q
  // Probe on EXT_p5
  // SwitchDT switchdt_1: pin names not known; wires that end beside it: clk, button_1_out, CLKR
  // Probe on RF_Q
  // DUMP DUMP: pin names not known; wires that end beside it: DIRECT_WE, ADDR_16[15:8], BUS_D, CLK_t, DUMP_p5
  or or_1 (or_1_out, ASSERT_p5, and_3_out, and_4_out);
  // Probe on DUMP_p5
  reg__sync_clear #(.generic("Bits := 8;")) WR (.D(BUS_D), .CLK(CLK_t), .nRST(CLR), .nLE(WR_WE), .Q(ADDR_16[7:0]));
  reg__sync_clear #(.generic("Bits := 8;")) SR (.D(BUS_D), .CLK(CLK_t), .nRST(CLR), .nLE(SR_WE), .Q(ADDR_16[15:8]));
  and and_5 (DIRECT_WE, RF_SFR, RAM_WE);
  and and_6 (DIRECT_OE, RF_SFR, RAM_OE);
  STALL STALL (.C(CLKR), .AC(or_1_out), .S(in_4), .OAC(CLK_t));  // open: G, nCLR, O
  INT INT (
    .CLK(CLK_t), .CLR(CLR), .A(ADDR_16[15:8]), .D(BUS_D), .WE(DIRECT_WE), .OE(DIRECT_OE), .IRQOE(IRQ_OE),
    .CII(IRQ_CLR));  // open: RI, TI, IRQ
  // Probe on ADDR_16[7:0]
  // Probe on ADDR_16[15:8]
  not not_13 (not_13_out, nROM_OE);
  ALU ALU (
    .A(RF_Q), .B(ADDR_16[7:0]), .S(ALUSD_FUNC), .CI(BR_Q), .nSOE(ALUS_OE), .nDLOE(ALUDL_OE),
    .nDHOE(ALUDH_OE), .O(BUS_D), .CO(ALUD_CO));
  ROM #(.AddrBits(16), .Bits(8)) ROM (.A(ADDR_16), .sel(not_13_out), .D(BUS_D));
  RAM RAM (.AC(CLK_t), .A(ADDR_16[15:8]), .WE(RAM_WE), .nOE(nRAM_OE), .Dt(RF_SFR), .O(BUS_D));
  XRAM XRAM (.CLKA(CLK_t), .A(ADDR_16), .WE(XRAM_WE), .nOE(nXRAM_OE), .O(BUS_D));
  BR BR (.CLK(CLK_t), .CLR(nCLR), .S(BR_SRC), .ALUDF(ALUD_CO), .ALUSF(ALUD_CO), .A0(RF_Q[0]), .A7(RF_Q[7]), .Q(BR_Q));
  // Pins of 1 and 8 bits meet at IMMED
  // Pins of 1 and 8 bits meet at BUS_D

  // Other names for the same wires on the sheet: ADDR_RAM[7:0] = ADDR_16[15:8]; GO = in_4

  // Notes on the sheet:
  //   clk: Hz: 2147483647
  //   LS137/LS138
  //   LS161
  //   LS151/LS251
  //   contents of DECODER_2 (hex, n*v repeats v):
  //   eef100488,100889,33a,105106,3830b5,3c54b8,3c08b9,20086e00000a,3002c600000a,38010e00000a,
  //   3c009e00000a,3e003e00000a,100485,34088a,eb0910086,3d007600000a,3d805600000a,100485,
  //   30088a,a00,eb0910086,3d407200000a,b3c,c800c,100486,1530c0,3c50b8,eb0bc00b9,eb0b80136,
  //   3c808e00000a,100485,30088a,600,980,eb0920086,3c0e8100000a,100481,100882,eb0920086,
  //   3a00ae00000a,100485,34088a,eb0800236,3900e600000a,3980c600000a,100485,30088a,a00,
  //   eb0800236,3940e200000a,b3c,c800c,640,1430b6,3c50b8,eb0bc00b9,eb08001b6,3880fe00000a,
  //   100485,30088a,600,980,eb08002b6,380e6900000a,100481,100882,eb08002b6,34020600000a,
  //   36014200000a,33c,100485,34088a,23d,25003d,4eaa00300d,10348c,850b8,3c20b9,658c,eb08c00b9,
  //   3501a600000a,35816a00000a,100485,30088a,a00,23c,100486,1d008c,10048c,eb09c00b6,35419200000a,
  //   b3c,c800c,640,1400bd,24043d,1500c0,4ea200358d,3c54b8,858bc08b9,405,450b6,1a2803000,
  //   eb0800000,eb0b00035,3481de00000a,34c1b600000a,3000,eb0b00035,73c,1400bd,2c003d,28083c,
  //   c800c,3640,18048d,1530c0,3c50b8,eb0bc00b9,340e8100000a,33c,100880,600,10088c,c800c,
  //   1500c0,243030,3c50b8,eb0bc00b9,32021e00000a,100485,34088a,600,110086,eb09400b6,31026e00000a,
  //   31823e00000a,100485,30088a,a00,100486,236,eb0950080,31426a00000a,b3c,c800c,640,1400bc,
  //   100486,1500c0,10048c,1430b6,3c50b8,eb0bc00b9,eb0bc0036,3082a600000a,30c27e00000a,
  //   2000,eb0b00035,73c,1400bd,2c003d,28083c,c800c,2640,18048d,1530c0,3c50b8,eb0bc00b9,
  //   300e6900000a,b3c,c800c,640,200830,153080,3c50b8,eb0bc00b9,2805be00000a,2c03f600000a,
  //   2e02fe00000a,33d,100485,34088a,23c,10248d,c54bc,300035,14510c,4ea2803580,3c54b8,858bc08b9,
  //   2d038200000a,2d833600000a,33d,100485,30088a,a00,23c,10248d,c54bc,300035,14510c,4ea2803580,
  //   3c54b8,858bc08b9,2d436200000a,b3c,c800c,2640,c5486,300035,1400bc,14510c,4ea2803580,
  //   3c54b8,858bc08b9,2700,c5486,300035,1400bc,14510c,4ea2803580,3c54b8,858bc08b9,2c83c200000a,
  //   2cc39200000a,385105,eb0b00035,73c,1400bd,2c003d,28083c,c800c,640,1c510d,1000,18048d,
  //   1530c0,3c50b8,eb0bc00b9,2c0e8100000a,73c,1400bd,2c003d,28083c,c800c,640,1c013d,38050d,
  //   345105,303035,3c50b8,eb0bc00b9,2a041e00000a,b3c,c800c,640,1400bc,100485,34088a,11308c,
  //   3c50b8,eb0bc00b9,29054e00000a,29844e00000a,b3c,c800c,640,1400bc,100485,30088a,a00,
  //   11308c,3c50b8,eb0bc00b9,29445200000a,21bc,44f6187036,82407,850bc,18703c,18203d,4502187036,
  //   82407,850bc,18703c,18203d,450a187036,82407,850bc,18703c,18203d,4512187036,82407,850bc,
  //   18703c,18203d,451a187036,82407,850bc,18703c,18203d,4522187036,82407,850bc,18703c,
  //   18203d,452a187036,82407,850bc,18703c,18203d,4532187036,82407,850bc,18743c,53898203d,
  //   1b6,21b7,eb0ac00b5,18703c,18203d,18703c,18203d,18703c,18203d,18703c,18203d,18703c,
  //   18203d,18703c,18203d,18743c,18203d,1400b7,145107,10148d,1400b6,eb0ac00b5,28858a00000a,
  //   28c56200000a,3000,3c50b1,eb0bc00b2,73c,1400bd,2c003d,28083c,c800c,640,1c510d,303035,
  //   3c50b8,eb0bc00b9,280e6900000a,73c,1400bd,2c003d,28083c,c800c,640,1c013d,38050d,305105,
  //   303035,3c50b8,eb0bc00b9,2406c200000a,2605ea00000a,106485,34088a,63d,c0506,1400bc,
  //   40c,2400b5,10048d,eb08c00b6,25066a00000a,25861a00000a,106485,30088a,a00,63d,c0506,
  //   1400bc,40c,2400b5,10048d,eb08c00b6,25464a00000a,6005,b3c,c800c,640,1400bd,c0506,1400bc,
  //   40c,2400b5,10048d,ea88c30b6,6005,73d,c0506,1400bc,40c,2400b5,10048d,ea88c30b6,2486ae00000a,
  //   24c68200000a,102486,85481,3c0882,eb0800336,6005,73c,1400bd,2c003d,28083c,c800c,640,
  //   18048d,1530c0,3c50b8,eb0bc00b9,240e8100000a,3332,3c54b8,3c08b9,ea8803331,2206e200000a,
  //   33c,100485,34088a,600,c800c,10088c,ea89530c0,21081200000a,21871200000a,33c,100485,
  //   30088a,a00,600,c800c,10088c,1530c0,3c50b8,eb0bc00b9,21473e00000a,b3c,c800c,640,1430bd,
  //   3c54b8,3c08b9,b3c,10048d,c800c,ea89530c0,1bc,480a102487,48021c6036,1c203c,c508c,75a802000,
  //   c30bc,1c6036,1c203c,c508c,76e802000,c30bc,1c6036,1c203c,c508c,782802000,c30bc,1c6036,
  //   1c203c,c508c,796802000,c30bc,1c6036,1c203c,c508c,7aa802000,c30bc,1c6036,1c203c,c508c,
  //   7be802000,c30bc,1c6036,1c203c,c508c,7d2802000,c30bc,1c6036,1c203c,c508c,7f2802000,
  //   c34bc,1400b7,1c2036,eb0ac00b5,10048c,1400b7,1c2036,eb0ac00b5,21b7,eb0ac00b5,3000,
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  //   at28c64
  //   core is at28c64
  //   contents of ROM (hex, n*v repeats v):
  //   75,d0,0,75,0,ff,76,0,75,0,fe,76,0,75,0,fd,76,0,75,0,fc,76,0,75,0,fb,76,0,75,0,fa,
  //   76,0,75,0,f9,76,0,75,0,f8,76,0,75,0,f7,76,0,75,0,f6,76,0,75,0,f5,76,0,75,0,f4,76,
  //   0,75,0,f3,76,0,75,0,f2,76,0,75,0,f1,76,0,75,0,f0,76,0,75,0,ef,76,0,75,0,ee,76,0,75,
  //   0,ed,76,0,75,0,ec,76,0,75,0,eb,76,0,75,0,ea,76,0,75,0,e9,76,0,75,0,e8,76,0,75,0,e7,
  //   76,0,75,0,e6,76,0,75,0,e5,76,0,75,0,e4,76,0,75,0,e3,76,0,75,0,e2,76,0,75,0,e1,76,
  //   0,75,0,e0,76,0,75,0,df,76,0,75,0,de,76,0,75,0,dd,76,0,75,0,dc,76,0,75,0,db,76,0,75,
  //   0,da,76,0,75,0,d9,76,0,75,0,d8,76,0,75,0,d7,76,0,75,0,d6,76,0,75,0,d5,76,0,75,0,d4,
  //   76,0,75,0,d3,76,0,75,0,d2,76,0,75,0,d1,76,0,75,0,d0,76,0,75,0,cf,76,0,75,0,ce,76,
  //   0,75,0,cd,76,0,75,0,cc,76,0,75,0,cb,76,0,75,0,ca,76,0,75,0,c9,76,0,75,0,c8,76,0,75,
  //   0,c7,76,0,75,0,c6,76,0,75,0,c5,76,0,75,0,c4,76,0,75,0,c3,76,0,75,0,c2,76,0,75,0,c1,
  //   76,0,75,0,c0,76,0,75,0,bf,76,0,75,0,be,76,0,75,0,bd,76,0,75,0,bc,76,0,75,0,bb,76,
  //   0,75,0,ba,76,0,75,0,b9,76,0,75,0,b8,76,0,75,0,b7,76,0,75,0,b6,76,0,75,0,b5,76,0,75,
  //   0,b4,76,0,75,0,b3,76,0,75,0,b2,76,0,75,0,b1,76,0,75,0,b0,76,0,75,0,af,76,0,75,0,ae,
  //   76,0,75,0,ad,76,0,75,0,ac,76,0,75,0,ab,76,0,75,0,aa,76,0,75,0,a9,76,0,75,0,a8,76,
  //   0,75,0,a7,76,0,75,0,a6,76,0,75,0,a5,76,0,75,0,a4,76,0,75,0,a3,76,0,75,0,a2,76,0,75,
  //   0,a1,76,0,75,0,a0,76,0,75,0,9f,76,0,75,0,9e,76,0,75,0,9d,76,0,75,0,9c,76,0,75,0,9b,
  //   76,0,75,0,9a,76,0,75,0,99,76,0,75,0,98,76,0,75,0,97,76,0,75,0,96,76,0,75,0,95,76,
  //   0,75,0,94,76,0,75,0,93,76,0,75,0,92,76,0,75,0,91,76,0,75,0,90,76,0,75,0,8f,76,0,75,
  //   0,8e,76,0,75,0,8d,76,0,75,0,8c,76,0,75,0,8b,76,0,75,0,8a,76,0,75,0,89,76,0,75,0,88,
  //   76,0,75,0,87,76,0,75,0,86,76,0,75,0,85,76,0,75,0,84,76,0,75,0,83,76,0,75,0,82,76,
  //   0,75,0,81,76,0,75,0,80,76,0,75,0,7f,76,0,75,0,7e,76,0,75,0,7d,76,0,75,0,7c,76,0,75,
  //   0,7b,76,0,75,0,7a,76,0,75,0,79,76,0,75,0,78,76,0,75,0,77,76,0,75,0,76,76,0,75,0,75,
  //   76,0,75,0,74,76,0,75,0,73,76,0,75,0,72,76,0,75,0,71,76,0,75,0,70,76,0,75,0,6f,76,
  //   0,75,0,6e,76,0,75,0,6d,76,0,75,0,6c,76,0,75,0,6b,76,0,75,0,6a,76,0,75,0,69,76,0,75,
  //   0,68,76,0,75,0,67,76,0,75,0,66,76,0,75,0,65,76,0,75,0,64,76,0,75,0,63,76,0,75,0,62,
  //   76,0,75,0,61,76,0,75,0,60,76,0,75,0,5f,76,0,75,0,5e,76,0,75,0,5d,76,0,75,0,5c,76,
  //   0,75,0,5b,76,0,75,0,5a,76,0,75,0,59,76,0,75,0,58,76,0,75,0,57,76,0,75,0,56,76,0,75,
  //   0,55,76,0,75,0,54,76,0,75,0,53,76,0,75,0,52,76,0,75,0,51,76,0,75,0,50,76,0,75,0,4f,
  //   76,0,75,0,4e,76,0,75,0,4d,76,0,75,0,4c,76,0,75,0,4b,76,0,75,0,4a,76,0,75,0,49,76,
  //   0,75,0,48,76,0,75,0,47,76,0,75,0,46,76,0,75,0,45,76,0,75,0,44,76,0,75,0,43,76,0,75,
  //   0,42,76,0,75,0,41,76,0,75,0,40,76,0,75,0,3f,76,0,75,0,3e,76,0,75,0,3d,76,0,75,0,3c,
  //   76,0,75,0,3b,76,0,75,0,3a,76,0,75,0,39,76,0,75,0,38,76,0,75,0,37,76,0,75,0,36,76,
  //   0,75,0,35,76,0,75,0,34,76,0,75,0,33,76,0,75,0,32,76,0,75,0,31,76,0,75,0,30,76,0,75,
  //   0,2f,76,0,75,0,2e,76,0,75,0,2d,76,0,75,0,2c,76,0,75,0,2b,76,0,75,0,2a,76,0,75,0,29,
  //   76,0,75,0,28,76,0,75,0,27,76,0,75,0,26,76,0,75,0,25,76,0,75,0,24,76,0,75,0,23,76,
  //   0,75,0,22,76,0,75,0,21,76,0,75,0,20,76,0,75,0,1f,76,0,75,0,1e,76,0,75,0,1d,76,0,75,
  //   0,1c,76,0,75,0,1b,76,0,75,0,1a,76,0,75,0,19,76,0,75,0,18,76,0,75,0,17,76,0,75,0,16,
  //   76,0,75,0,15,76,0,75,0,14,76,0,75,0,13,76,0,75,0,12,76,0,75,0,11,76,0,75,0,10,76,
  //   0,75,0,f,76,0,75,0,e,76,0,75,0,d,76,0,75,0,c,76,0,75,0,b,76,0,75,0,a,76,0,75,0,9,
  //   76,0,75,0,8,76,0,75,0,7,76,0,75,0,6,76,0,75,0,5,76,0,75,0,4,76,0,75,0,3,76,0,75,0,
  //   2,76,0,75,0,1,76,0,75,0,0,76,0,75,81,0,75,82,0,75,83,0,75,d0,0,75,e0,0,75,f0,0,75,
  //   82,51,75,83,88,75,e0,45,f0,75,82,b8,75,83,92,75,e0,84,f0,75,82,f4,75,83,8b,75,e0,
  //   63,f0,75,82,87,75,83,5d,75,e0,6f,f0,75,82,c,75,83,1a,75,e0,aa,f0,75,82,f1,75,83,eb,
  //   75,e0,3e,f0,75,82,97,75,83,7,75,e0,f4,f0,75,82,9c,75,83,74,75,e0,4d,f0,75,82,b9,75,
  //   83,8f,75,e0,ae,f0,75,82,61,75,83,54,75,e0,7a,f0,75,82,f0,75,83,6d,75,e0,a,f0,75,82,
  //   46,75,83,1e,75,e0,f7,f0,75,82,1e,75,83,cd,75,e0,e1,f0,75,82,cc,75,83,fa,75,e0,e2,
  //   f0,75,82,a9,75,83,39,75,e0,ea,f0,75,82,4,75,83,3c,75,e0,da,f0,75,82,63,75,83,e,75,
  //   e0,59,f0,75,82,e5,75,83,a6,75,e0,c,f0,75,82,42,75,83,76,75,e0,e0,f0,75,82,a6,75,83,
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  //   core is 6116
  //   L74+LS252
endmodule
