// Digital circuit DCOUTER.dig as structural Verilog
module DCOUTER (
  input  CLK,
  input  CLR,
  input  CNT,
  input  LE,
  input  [11:0] D,
  output [11:0] Q
);

  wire or_1_out;
  wire [11:0] add_1_s, reg__sync_clear_1_p1;

  or or_1 (or_1_out, CNT, LE);
  // reg__sync_clear #(.generic("Bits := args.Bits;")) reg__sync_clear_1: pin names not known; wires that end beside it: reg__sync_clear_1_p1, CLK, CLR, or_1_out, Q
  Add #(.Bits(12), .generic("Bits := int(args.Bits);")) add_1 (.a(12'h1), .b(Q), .c_i(1'b0), .s(add_1_s));  // open: c_o
  Multiplexer #(.Bits(12), .generic("Bits := int(args.Bits);")) multiplexer_1 (
    .sel(LE), .in_0(add_1_s), .in_1(D), .out(reg__sync_clear_1_p1));

  // Notes on the sheet:
  //   CNT: Q = Q + 1, lower priority than LE
  //   LE: load value from D
endmodule
