// Digital circuit INT.dig as structural Verilog
// PC external, for debug purpose, laod PC from RF to this register.
// select byte PCEL when RS is 8, select byte PCEH when RS is 9.
module INT (
  input  CLK,
  input  CLR,
  input  [7:0] A,
  input  [7:0] D,
  input  WE,
  input  OE,
  input  nIRQ_OE,
  input  CAI,
  input  RI,
  input  TI,
  output [7:0] IRQ
);

  wire and_1_out, and_2_out, comparator_1_eq;
  wire [7:0] TCON_q;

  Comparator #(.Bits(8)) comparator_1 (.a(A), .b(8'h88), .eq(comparator_1_eq));  // open: gt, lt
  and and_1 (and_1_out, WE, comparator_1_eq);
  and and_2 (and_2_out, comparator_1_eq, OE);
  INT_TCON TCON (.D(D), .WE(and_1_out), .CII(CAI), .CLK(CLK), .CLR(CLR), .IRQ(IRQ[3:0]), .Q(TCON_q));
  SCON SCON (.CLK(CLK), .CLR(CLR), .IO(D), .A(A), .OE(OE), .WE(WE), .RI(RI), .TI(TI), .TRI(IRQ[4]));
  assign D = and_2_out ? TCON_q : 8'bz;  // Driver driver_1
  assign D = ~nIRQ_OE ? {3'b000, IRQ[4:0]} : 8'bz;  // DriverInvSel driverinvsel_1

  assign IRQ[7:5] = 3'b000;

  // Notes on the sheet:
  //   nIRQ_OE: default 1
  //   CAI: clear accepted interrupt
endmodule
