// Digital circuit PER_INT_IO.dig as structural Verilog
// interrupt, IO:
// UART: SBUF, SCON
// external int: TCON
module PER_INT_IO (
  input  CLK,
  input  nRST,
  input  [7:0] A,
  input  [7:0] D,
  input  nWE,
  input  nOE,
  input  [7:0] nIRR_CLRB,
  output [7:0] IRR_Q
);

  wire sfr_ctl_1_noe, sfr_ctl_1_nwe, sfr_ctl_2_noe, sfr_ctl_2_nwe, sfr_ctl_3_noe, sfr_ctl_3_nwe;
  wire [1:0] sfr_sbuf_1_ri;

  SFR_CTL sfr_ctl_1 (.nSFR_WE(nWE), .nSFR_OE(nOE), .A(A), .MADDR(8'h88), .nWE(sfr_ctl_1_nwe), .nOE(sfr_ctl_1_noe));
  SFR_CTL sfr_ctl_2 (.nSFR_WE(nWE), .nSFR_OE(nOE), .A(A), .MADDR(8'h98), .nWE(sfr_ctl_2_nwe), .nOE(sfr_ctl_2_noe));
  SFR_CTL sfr_ctl_3 (.nSFR_WE(nWE), .nSFR_OE(nOE), .A(A), .MADDR(8'h99), .nWE(sfr_ctl_3_nwe), .nOE(sfr_ctl_3_noe));
  SFR_TCON sfr_tcon_1 (
    .CLK(CLK), .nRST(nRST), .D(D), .nWE(sfr_ctl_1_nwe), .nOE(sfr_ctl_1_noe), .IRQ(4'b0000),
    .nIRR_CB(nIRR_CLRB[3:0]), .IRRQ(IRR_Q[3:0]));  // open: Q
  SFR_SCON sfr_scon_1 (
    .CLK(CLK), .nRST(nRST), .D(D), .nWE(sfr_ctl_2_nwe), .nOE(sfr_ctl_2_noe), .IRQ(sfr_sbuf_1_ri),
    .IRRQ(IRR_Q[4]));  // open: Q
  SFR_SBUF sfr_sbuf_1 (
    .CLK(CLK), .D(D), .nWE(sfr_ctl_3_nwe), .nOE(sfr_ctl_3_noe), .RI(sfr_sbuf_1_ri[0]), .TI(sfr_sbuf_1_ri[1]));

  assign IRR_Q[7:5] = 3'b000;

  // Other names for the same wires on the sheet: ADDR_SFR[7:0] = A; BUS_D[7:0] = D; nSFR_OE = nOE; nSFR_WE = nWE

  // Notes on the sheet:
  //   A: address input
  //   D: Data Bus
  //   nWE: write enable
  //   The SFR in the corresponding address will read the data from  the data bus.
  //   nOE: ouput enable.
  //   The SFR in the corresponding address will drive the data  bus.
endmodule
