// Digital circuit reg-file.dig as structural Verilog
module reg_file (
  input  CLK,
  input  [3:0] RS,
  input  [7:0] D,
  input  LE,
  output [7:0] Q
);

  wire [7:0] multiplexer_1_out;

  Multiplexer #(.Bits(8)) multiplexer_1 (.sel(LE), .in_0(Q), .in_1(D), .out(multiplexer_1_out));
  RAMDualPort #(.AddrBits(4), .Bits(8)) RF (.A(RS), .Din(multiplexer_1_out), .str(1'b1), .C(CLK), .ld(1'b1), .D(Q));
endmodule
